// Logisim project basic-gates.circ as structural Verilog: 5 circuits, main circuit not
module \not  (
  input  \input ,
  output \output 
);

  nand NOT (\output , \input , \input );
endmodule

module \and  (
  input  a,
  input  b,
  output out
);

  wire nand_1_out, nand_2_out;

  nand nand_1 (nand_1_out, a, b);
  nand nand_2 (nand_2_out, a, b);
  nand nand_3 (out, nand_1_out, nand_2_out);
endmodule

module \or  (
  input  a,
  input  b,
  output out
);

  wire not_1_output, not_2_output;

  \not  not_1 (.\input (a), .\output (not_1_output));
  \not  not_2 (.\input (b), .\output (not_2_output));
  nand nand_1 (out, not_1_output, not_2_output);
endmodule

module \xor  (
  input  a,
  input  b,
  output out_3
);

  wire nand_1_out, or_1_out;

  \or  or_1 (.a(a), .b(b), .out(or_1_out));
  nand nand_1 (nand_1_out, a, b);
  \and  and_1 (.a(or_1_out), .b(nand_1_out), .out(out_3));
endmodule

module \nor  (
  input  a,
  input  b,
  output out
);

  wire or_1_out;

  \or  or_1 (.a(a), .b(b), .out(or_1_out));
  \not  not_1 (.\input (or_1_out), .\output (out));
endmodule
