// Logisim project sequential-logic.circ as structural Verilog
module rs_latch (
  input  r,
  input  s,
  output out,
  output not_out
);

  \nor  nor_1 (.a(r), .b(not_out), .out(out));
  \nor  nor_2 (.a(out), .b(s), .out(not_out));
endmodule

module d_latch (
  input  in,
  input  load,
  output out,
  output not_out
);

  wire and_1_out, and_2_out, not_1_output;

  \not  not_1 (.\input (in), .\output (not_1_output));
  \and  and_1 (.a(not_1_output), .b(load), .out(and_1_out));
  \and  and_2 (.a(in), .b(load), .out(and_2_out));
  rs_latch rs_latch_1 (.r(and_1_out), .s(and_2_out), .out(out), .not_out(not_out));

  // Notes on the sheet:
  //   reset
  //   set
endmodule

module d_latch_tmp (
  input  in_1,
  input  in_2,
  output out_3
);

  wire and_1_out, and_2_out, not_1_output;

  \not  not_1 (.\input (in_2), .\output (not_1_output));
  \and  and_1 (.a(in_1), .b(in_2), .out(and_1_out));
  \and  and_2 (.a(not_1_output), .b(out_3), .out(and_2_out));
  \or  or_1 (.a(and_1_out), .b(and_2_out), .out(out_3));
endmodule

module _8_bit_reg (
  input  clk,
  input  rd,
  input  wr,
  input  [7:0] in,
  output [7:0] out
);

  wire and_1_out, and_2_out, and_3_out, and_4_out, and_5_out, and_6_out, and_7_out, and_8_out, and_9_out,
       d_latch_1_out, d_latch_2_out, d_latch_3_out, d_latch_4_out, d_latch_5_out, d_latch_6_out,
       d_latch_7_out, d_latch_8_out;

  \and  and_1 (.a(clk), .b(wr), .out(and_1_out));
  d_latch d_latch_1 (.in(in[0]), .load(and_1_out), .out(d_latch_1_out));  // open: not_out
  d_latch d_latch_2 (.in(in[1]), .load(and_1_out), .out(d_latch_2_out));  // open: not_out
  d_latch d_latch_3 (.in(in[2]), .load(and_1_out), .out(d_latch_3_out));  // open: not_out
  d_latch d_latch_4 (.in(in[3]), .load(and_1_out), .out(d_latch_4_out));  // open: not_out
  d_latch d_latch_5 (.in(in[4]), .load(and_1_out), .out(d_latch_5_out));  // open: not_out
  d_latch d_latch_6 (.in(in[5]), .load(and_1_out), .out(d_latch_6_out));  // open: not_out
  d_latch d_latch_7 (.in(in[6]), .load(and_1_out), .out(d_latch_7_out));  // open: not_out
  d_latch d_latch_8 (.in(in[7]), .load(and_1_out), .out(d_latch_8_out));  // open: not_out
  \and  and_2 (.a(rd), .b(d_latch_1_out), .out(and_2_out));
  \and  and_3 (.a(rd), .b(d_latch_2_out), .out(and_3_out));
  \and  and_4 (.a(rd), .b(d_latch_3_out), .out(and_4_out));
  \and  and_5 (.a(rd), .b(d_latch_4_out), .out(and_5_out));
  \and  and_6 (.a(rd), .b(d_latch_5_out), .out(and_6_out));
  \and  and_7 (.a(rd), .b(d_latch_6_out), .out(and_7_out));
  \and  and_8 (.a(rd), .b(d_latch_7_out), .out(and_8_out));
  \and  and_9 (.a(rd), .b(d_latch_8_out), .out(and_9_out));
  \and  and_10 (.a(clk), .b(and_2_out), .out(out[0]));
  \and  and_11 (.a(clk), .b(and_3_out), .out(out[1]));
  \and  and_12 (.a(clk), .b(and_4_out), .out(out[2]));
  \and  and_13 (.a(clk), .b(and_5_out), .out(out[3]));
  \and  and_14 (.a(clk), .b(and_6_out), .out(out[4]));
  \and  and_15 (.a(clk), .b(and_7_out), .out(out[5]));
  \and  and_16 (.a(clk), .b(and_8_out), .out(out[6]));
  \and  and_17 (.a(clk), .b(and_9_out), .out(out[7]));

  // Notes on the sheet:
  //   clk = global clock
  //   rd = read output from reg
  //   wr = write input to reg
  //   clk ^ wr
  //   clk ^ out'
  //   out ^ rd
endmodule
